// Logisim project Guia-0607.circ as structural Verilog: 1 circuit, main circuit main
module main (
  input  x,
  input  y,
  input  z,
  output S
);

  wire not_1_out, not_2_out, or_1_out, or_2_out;

  not not_1 (not_1_out, y);
  not not_2 (not_2_out, x);
  or or_1 (or_1_out, x, not_1_out, z);
  or or_2 (or_2_out, not_2_out, y, z);
  and and_1 (S, or_1_out, or_2_out);

  // Notes on the sheet:
  //   Circuito siplificado:
endmodule
